// Digital circuit ALU Decoder.dig as structural Verilog
module ALU_Decoder (
  input  [2:0] i,
  output XOR,
  output OR,
  output AND,
  output NOT,
  output SHR,
  output SHL,
  output CMP,
  output ADD
);

  wire not_1_out, not_2_out, not_3_out, not_4_out, not_5_out, not_6_out, not_7_out, not_8_out, not_9_out,
       not_10_out, not_11_out, not_12_out;

  not not_1 (not_1_out, i[0]);
  not not_2 (not_2_out, i[1]);
  not not_3 (not_3_out, i[1]);
  not not_4 (not_4_out, i[0]);
  not not_5 (not_5_out, i[2]);
  not not_6 (not_6_out, i[2]);
  not not_7 (not_7_out, i[0]);
  not not_8 (not_8_out, i[2]);
  not not_9 (not_9_out, i[1]);
  not not_10 (not_10_out, i[2]);
  not not_11 (not_11_out, i[1]);
  not not_12 (not_12_out, i[0]);
  and and_1 (XOR, i[2], i[1], i[0]);
  and and_2 (OR, i[2], i[1], not_1_out);
  and and_3 (AND, i[2], not_2_out, i[0]);
  and and_4 (NOT, i[2], not_3_out, not_4_out);
  and and_5 (SHR, not_5_out, i[1], i[0]);
  and and_6 (SHL, not_6_out, i[1], not_7_out);
  and and_7 (CMP, not_8_out, not_9_out, i[0]);
  and and_8 (ADD, not_10_out, not_11_out, not_12_out);
endmodule
