// Digital circuit Accumulator.dig as structural Verilog
module Accumulator (
  input  s,
  input  e,
  input  [7:0] i,
  input  clk,
  output [7:0] o
);

  wire [7:0] _1_byte_register_1_o;

  _1_Byte_Register _1_byte_register_1 (.i(i), .clk(clk), .s(s), .o(_1_byte_register_1_o));
  _8_Bit_Switch _8_bit_switch_1 (.i(_1_byte_register_1_o), .e(e), .o(o));
endmodule
