// Digital circuit Bus 1.dig as structural Verilog
module Bus_1 (
  input  e,
  input  [7:0] i,
  output [7:0] o
);

  wire not_1_out;

  not not_1 (not_1_out, e);
  or or_1 (o[0], e, i[0]);
  and and_1 (o[1], not_1_out, i[1]);
  and and_2 (o[2], not_1_out, i[2]);
  and and_3 (o[3], not_1_out, i[3]);
  and and_4 (o[4], not_1_out, i[4]);
  and and_5 (o[5], not_1_out, i[5]);
  and and_6 (o[6], not_1_out, i[6]);
  and and_7 (o[7], not_1_out, i[7]);
endmodule
