// Digital circuit Flags.dig as structural Verilog
// sets on falling edge because it was updating before acc sent the data
module Flags (
  input  s,
  input  [3:0] i,
  input  clk,
  output [3:0] o
);

  wire and_1_out, not_1_out;

  and and_1 (and_1_out, not_1_out, s);
  not not_1 (not_1_out, clk);
  D_FF eq (.D(i[0]), .C(and_1_out), .Q(o[0]));  // open: nQ
  D_FF gt (.D(i[1]), .C(and_1_out), .Q(o[1]));  // open: nQ
  D_FF z (.D(i[2]), .C(and_1_out), .Q(o[2]));  // open: nQ
  D_FF c (.D(i[3]), .C(and_1_out), .Q(o[3]));  // open: nQ
endmodule
