// Digital circuit 8 Bit AND.dig as structural Verilog
module _8_Bit_AND (
  input  [7:0] i_1,
  input  [7:0] i_2,
  output [7:0] o
);

  and and_1 (o[0], i_1[0], i_2[0]);
  and and_2 (o[1], i_1[1], i_2[1]);
  and and_3 (o[2], i_1[2], i_2[2]);
  and and_4 (o[3], i_1[3], i_2[3]);
  and and_5 (o[4], i_1[4], i_2[4]);
  and and_6 (o[5], i_1[5], i_2[5]);
  and and_7 (o[6], i_1[6], i_2[6]);
  and and_8 (o[7], i_1[7], i_2[7]);
endmodule
