// Digital circuit 8 Bit Compare XOR.dig as structural Verilog
module _8_Bit_Compare_XOR (
  input  [7:0] i_1,
  input  [7:0] i_2,
  output [7:0] o,
  output eq,
  output gt
);

  wire compare_xor_1_eq, compare_xor_1_gt, compare_xor_2_eq, compare_xor_2_gt, compare_xor_3_eq,
       compare_xor_3_gt, compare_xor_4_eq, compare_xor_4_gt, compare_xor_5_eq, compare_xor_5_gt,
       compare_xor_6_eq, compare_xor_6_gt, compare_xor_7_eq, compare_xor_7_gt;

  Compare_XOR compare_xor_1 (
    .eq_p(1'b1), .gt_p(1'b0), .i_1(i_1[7]), .i_2(i_2[7]), .o(o[7]), .eq(compare_xor_1_eq),
    .gt(compare_xor_1_gt));
  Compare_XOR compare_xor_2 (
    .eq_p(compare_xor_1_eq), .gt_p(compare_xor_1_gt), .i_1(i_1[6]), .i_2(i_2[6]), .o(o[6]),
    .eq(compare_xor_2_eq), .gt(compare_xor_2_gt));
  Compare_XOR compare_xor_3 (
    .eq_p(compare_xor_2_eq), .gt_p(compare_xor_2_gt), .i_1(i_1[5]), .i_2(i_2[5]), .o(o[5]),
    .eq(compare_xor_3_eq), .gt(compare_xor_3_gt));
  Compare_XOR compare_xor_4 (
    .eq_p(compare_xor_3_eq), .gt_p(compare_xor_3_gt), .i_1(i_1[4]), .i_2(i_2[4]), .o(o[4]),
    .eq(compare_xor_4_eq), .gt(compare_xor_4_gt));
  Compare_XOR compare_xor_5 (
    .eq_p(compare_xor_4_eq), .gt_p(compare_xor_4_gt), .i_1(i_1[3]), .i_2(i_2[3]), .o(o[3]),
    .eq(compare_xor_5_eq), .gt(compare_xor_5_gt));
  Compare_XOR compare_xor_6 (
    .eq_p(compare_xor_5_eq), .gt_p(compare_xor_5_gt), .i_1(i_1[2]), .i_2(i_2[2]), .o(o[2]),
    .eq(compare_xor_6_eq), .gt(compare_xor_6_gt));
  Compare_XOR compare_xor_7 (
    .eq_p(compare_xor_6_eq), .gt_p(compare_xor_6_gt), .i_1(i_1[1]), .i_2(i_2[1]), .o(o[1]),
    .eq(compare_xor_7_eq), .gt(compare_xor_7_gt));
  Compare_XOR compare_xor_8 (
    .eq_p(compare_xor_7_eq), .gt_p(compare_xor_7_gt), .i_1(i_1[0]), .i_2(i_2[0]), .o(o[0]), .eq(eq), .gt(gt));
endmodule
