// Digital circuit 8 Bit Inverter.dig as structural Verilog
module _8_Bit_Inverter (
  input  [7:0] i,
  output [7:0] o
);

  not not_1 (o[0], i[0]);
  not not_2 (o[1], i[1]);
  not not_3 (o[2], i[2]);
  not not_4 (o[3], i[3]);
  not not_5 (o[4], i[4]);
  not not_6 (o[5], i[5]);
  not not_7 (o[6], i[6]);
  not not_8 (o[7], i[7]);
endmodule
