// Digital circuit 8 Bit OR.dig as structural Verilog
module _8_Bit_OR (
  input  [7:0] i_1,
  input  [7:0] i_2,
  output [7:0] o
);

  or or_1 (o[0], i_1[0], i_2[0]);
  or or_2 (o[1], i_1[1], i_2[1]);
  or or_3 (o[2], i_1[2], i_2[2]);
  or or_4 (o[3], i_1[3], i_2[3]);
  or or_5 (o[4], i_1[4], i_2[4]);
  or or_6 (o[5], i_1[5], i_2[5]);
  or or_7 (o[6], i_1[6], i_2[6]);
  or or_8 (o[7], i_1[7], i_2[7]);
endmodule
