// Digital circuit 8 Bit RCA.dig as structural Verilog
module _8_Bit_RCA (
  input  c_i,
  input  [7:0] i_1,
  input  [7:0] i_2,
  output [7:0] o,
  output c_o
);

  wire full_adder_1_c_o, full_adder_2_c_o, full_adder_3_c_o, full_adder_4_c_o, full_adder_5_c_o,
       full_adder_6_c_o, full_adder_7_c_o;

  Full_Adder full_adder_1 (.c_i(c_i), .i_1(i_1[0]), .i_2(i_2[0]), .s(o[0]), .c_o(full_adder_1_c_o));
  Full_Adder full_adder_2 (.c_i(full_adder_1_c_o), .i_1(i_1[1]), .i_2(i_2[1]), .s(o[1]), .c_o(full_adder_2_c_o));
  Full_Adder full_adder_3 (.c_i(full_adder_2_c_o), .i_1(i_1[2]), .i_2(i_2[2]), .s(o[2]), .c_o(full_adder_3_c_o));
  Full_Adder full_adder_4 (.c_i(full_adder_3_c_o), .i_1(i_1[3]), .i_2(i_2[3]), .s(o[3]), .c_o(full_adder_4_c_o));
  Full_Adder full_adder_5 (.c_i(full_adder_4_c_o), .i_1(i_1[4]), .i_2(i_2[4]), .s(o[4]), .c_o(full_adder_5_c_o));
  Full_Adder full_adder_6 (.c_i(full_adder_5_c_o), .i_1(i_1[5]), .i_2(i_2[5]), .s(o[5]), .c_o(full_adder_6_c_o));
  Full_Adder full_adder_7 (.c_i(full_adder_6_c_o), .i_1(i_1[6]), .i_2(i_2[6]), .s(o[6]), .c_o(full_adder_7_c_o));
  Full_Adder full_adder_8 (.c_i(full_adder_7_c_o), .i_1(i_1[7]), .i_2(i_2[7]), .s(o[7]), .c_o(c_o));
endmodule
