// Digital circuit 8 Bit Shift Left.dig as structural Verilog
module _8_Bit_Shift_Left (
  input  [7:0] i,
  input  s_i,
  output s_o,
  output [7:0] o
);


  assign o = {i[6:0], s_i};
  assign s_o = i[7];
endmodule
