// Digital circuit 8 Bit Shift Right.dig as structural Verilog
module _8_Bit_Shift_Right (
  input  s_i,
  input  [7:0] i,
  output [7:0] o,
  output s_o
);


  assign o = {s_i, i[7:1]};
  assign s_o = i[0];
endmodule
