// Digital circuit Compare XOR.dig as structural Verilog
module Compare_XOR (
  input  eq_p,
  input  gt_p,
  input  i_1,
  input  i_2,
  output o,
  output eq,
  output gt
);

  wire and_2_out, not_1_out;

  xor xor_1 (o, i_1, i_2);
  not not_1 (not_1_out, o);
  and and_1 (eq, eq_p, not_1_out);
  and and_2 (and_2_out, eq_p, i_1, o);
  or or_1 (gt, gt_p, and_2_out);
endmodule
