// Digital circuit Full Adder.dig as structural Verilog
module Full_Adder (
  input  c_i,
  input  i_1,
  input  i_2,
  output s,
  output c_o
);

  wire half_adder_1_c, half_adder_1_s, half_adder_2_c;

  Half_Adder half_adder_1 (.i_1(i_1), .i_2(i_2), .s(half_adder_1_s), .c(half_adder_1_c));
  Half_Adder half_adder_2 (.i_1(c_i), .i_2(half_adder_1_s), .s(s), .c(half_adder_2_c));
  or or_1 (c_o, half_adder_2_c, half_adder_1_c);
endmodule
