// Digital circuit ALU programmer.dig as structural Verilog
module ALU_programmer (
  input  CMP,
  input  ADD,
  input  SHR,
  input  SHL,
  input  NOT,
  input  AND,
  input  OR,
  input  XOR,
  input  e,
  output [3:0] o
);

  wire [0:0] not_12_out;
  wire [1:0] not_9_out;
  wire [1:1] not_11_out;
  wire [2:0] _3_bit_switch_1_o, not_1_out, not_6_out;
  wire [2:1] not_4_out;
  wire [2:2] not_8_out;

  not not_1 (not_1_out[0], 1'b1);
  not not_2 (not_1_out[1], 1'b1);
  not not_3 (not_1_out[2], 1'b1);
  not not_4 (not_4_out[1], 1'b1);
  not not_5 (not_4_out[2], 1'b1);
  not not_6 (not_6_out[0], 1'b1);
  not not_7 (not_6_out[2], 1'b1);
  not not_8 (not_8_out[2], 1'b1);
  not not_9 (not_9_out[0], 1'b1);
  not not_10 (not_9_out[1], 1'b1);
  not not_11 (not_11_out[1], 1'b1);
  not not_12 (not_12_out[0], 1'b1);
  _3_Bit_Switch _3_bit_switch_1 (.i(not_1_out), .e(CMP), .o(_3_bit_switch_1_o));
  _3_Bit_Switch _3_bit_switch_2 (.i({not_4_out, 1'b1}), .e(ADD), .o(_3_bit_switch_1_o));
  _3_Bit_Switch _3_bit_switch_3 (.i({not_6_out[2], 1'b1, not_6_out[0]}), .e(SHR), .o(_3_bit_switch_1_o));
  _3_Bit_Switch _3_bit_switch_4 (.i({not_8_out[2], 2'b11}), .e(SHL), .o(_3_bit_switch_1_o));
  _3_Bit_Switch _3_bit_switch_5 (.i({1'b1, not_9_out}), .e(NOT), .o(_3_bit_switch_1_o));
  _3_Bit_Switch _3_bit_switch_6 (.i({1'b1, not_11_out[1], 1'b1}), .e(AND), .o(_3_bit_switch_1_o));
  _3_Bit_Switch _3_bit_switch_7 (.i({2'b11, not_12_out[0]}), .e(OR), .o(_3_bit_switch_1_o));
  _3_Bit_Switch _3_bit_switch_8 (.i(3'b111), .e(XOR), .o(_3_bit_switch_1_o));
  _4_Bit_Switch _4_bit_switch_1 (.i({1'b1, _3_bit_switch_1_o}), .e(e), .o(o));
endmodule
