// Digital circuit Instruction Register.dig as structural Verilog
module Instruction_Register (
  input  [7:0] i,
  input  clk,
  input  s,
  output [7:0] o
);

  wire and_1_out;

  and and_1 (and_1_out, clk, s);
  _1_Byte_Memory _1_byte_memory_1 (.i(i), .c(and_1_out), .o(o));
endmodule
