// Digital circuit load instruction decoder.dig as structural Verilog
module load_instruction_decoder (
  input  [2:0] i,
  input  e,
  output clr_f,
  output ld,
  output str,
  output mov_i,
  output jmp_r,
  output jmp_a,
  output jmp_c,
  output nop
);

  wire not_1_out, not_2_out, not_3_out, not_4_out, not_5_out, not_6_out, not_7_out, not_8_out, not_9_out,
       not_10_out, not_11_out, not_12_out;

  not not_1 (not_1_out, i[2]);
  not not_2 (not_2_out, i[1]);
  not not_3 (not_3_out, i[0]);
  not not_4 (not_4_out, i[2]);
  not not_5 (not_5_out, i[1]);
  not not_6 (not_6_out, i[2]);
  not not_7 (not_7_out, i[0]);
  not not_8 (not_8_out, i[2]);
  not not_9 (not_9_out, i[1]);
  not not_10 (not_10_out, i[0]);
  not not_11 (not_11_out, i[1]);
  not not_12 (not_12_out, i[0]);
  and and_1 (clr_f, not_1_out, not_2_out, not_3_out, e);
  and and_2 (ld, not_4_out, not_5_out, i[0], e);
  and and_3 (str, not_6_out, i[1], not_7_out, e);
  and and_4 (mov_i, not_8_out, i[1], i[0], e);
  and and_5 (jmp_r, i[2], not_9_out, not_10_out, e);
  and and_6 (jmp_a, i[2], not_11_out, i[0], e);
  and and_7 (jmp_c, i[2], i[1], not_12_out, e);
  and and_8 (nop, i[2], i[1], i[0], e);
endmodule
