// Digital circuit 2 Bit Decoder.dig as structural Verilog
module _2_Bit_Decoder (
  input  [1:0] i,
  input  e,
  output _00,
  output _01,
  output _10,
  output _11
);

  wire not_1_out, not_2_out, not_3_out, not_4_out;

  not not_1 (not_1_out, i[0]);
  not not_2 (not_2_out, i[1]);
  not not_3 (not_3_out, i[0]);
  not not_4 (not_4_out, i[1]);
  and and_1 (_11, i[0], i[1], e);
  and and_2 (_10, not_1_out, i[1], e);
  and and_3 (_01, i[0], not_2_out, e);
  and and_4 (_00, not_3_out, not_4_out, e);
endmodule
