// Digital circuit 3 Bit Decoder.dig as structural Verilog
module _3_Bit_Decoder (
  input  [2:0] i,
  output _111,
  output _110,
  output _101,
  output _100,
  output _011,
  output _010,
  output _001,
  output _000
);

  wire not_1_out, not_2_out, not_3_out, not_4_out, not_5_out, not_6_out, not_7_out, not_8_out, not_9_out,
       not_10_out, not_11_out, not_12_out;

  not not_1 (not_1_out, i[0]);
  not not_2 (not_2_out, i[1]);
  not not_3 (not_3_out, i[1]);
  not not_4 (not_4_out, i[0]);
  not not_5 (not_5_out, i[2]);
  not not_6 (not_6_out, i[2]);
  not not_7 (not_7_out, i[0]);
  not not_8 (not_8_out, i[2]);
  not not_9 (not_9_out, i[1]);
  not not_10 (not_10_out, i[2]);
  not not_11 (not_11_out, i[1]);
  not not_12 (not_12_out, i[0]);
  and and_1 (_111, i[2], i[1], i[0]);
  and and_2 (_110, i[2], i[1], not_1_out);
  and and_3 (_101, i[2], not_2_out, i[0]);
  and and_4 (_100, i[2], not_3_out, not_4_out);
  and and_5 (_011, not_5_out, i[1], i[0]);
  and and_6 (_010, not_6_out, i[1], not_7_out);
  and and_7 (_001, not_8_out, not_9_out, i[0]);
  and and_8 (_000, not_10_out, not_11_out, not_12_out);
endmodule
