// Digital circuit 4 Bit Decoder.dig as structural Verilog
module _4_Bit_Decoder (
  input  [3:0] i,
  output _0000,
  output _0001,
  output _0010,
  output _0011,
  output _0100,
  output _0101,
  output _0110,
  output _0111,
  output _1000,
  output _1001,
  output _1010,
  output _1011,
  output _1100,
  output _1101,
  output _1110,
  output _1111
);

  wire not_1_out, not_2_out, not_3_out, not_4_out, not_5_out, not_6_out, not_7_out, not_8_out, not_9_out,
       not_10_out, not_11_out, not_12_out, not_13_out, not_14_out, not_15_out, not_16_out, not_17_out,
       not_18_out, not_19_out, not_20_out, not_21_out, not_22_out, not_23_out, not_24_out, not_25_out,
       not_26_out, not_27_out, not_28_out, not_29_out, not_30_out, not_31_out, not_32_out;

  and and_1 (_1111, i[0], i[1], i[2], i[3]);
  and and_2 (_1110, not_1_out, i[1], i[2], i[3]);
  and and_3 (_1101, i[0], not_2_out, i[2], i[3]);
  and and_4 (_1100, not_4_out, not_3_out, i[2], i[3]);
  and and_5 (_1011, i[0], i[1], not_5_out, i[3]);
  and and_6 (_1010, not_7_out, i[1], not_6_out, i[3]);
  and and_7 (_1001, i[0], not_9_out, not_8_out, i[3]);
  and and_8 (_1000, not_12_out, not_11_out, not_10_out, i[3]);
  not not_1 (not_1_out, i[0]);
  not not_2 (not_2_out, i[1]);
  not not_3 (not_3_out, i[1]);
  not not_4 (not_4_out, i[0]);
  not not_5 (not_5_out, i[2]);
  not not_6 (not_6_out, i[2]);
  not not_7 (not_7_out, i[0]);
  not not_8 (not_8_out, i[2]);
  not not_9 (not_9_out, i[1]);
  not not_10 (not_10_out, i[2]);
  not not_11 (not_11_out, i[1]);
  not not_12 (not_12_out, i[0]);
  not not_13 (not_13_out, i[3]);
  not not_14 (not_14_out, i[3]);
  not not_15 (not_15_out, i[0]);
  not not_16 (not_16_out, i[3]);
  not not_17 (not_17_out, i[1]);
  not not_18 (not_18_out, i[3]);
  not not_19 (not_19_out, i[1]);
  not not_20 (not_20_out, i[0]);
  not not_21 (not_21_out, i[3]);
  not not_22 (not_22_out, i[2]);
  not not_23 (not_23_out, i[3]);
  not not_24 (not_24_out, i[2]);
  not not_25 (not_25_out, i[0]);
  not not_26 (not_26_out, i[3]);
  not not_27 (not_27_out, i[2]);
  not not_28 (not_28_out, i[1]);
  not not_29 (not_29_out, i[3]);
  not not_30 (not_30_out, i[2]);
  not not_31 (not_31_out, i[1]);
  not not_32 (not_32_out, i[0]);
  and and_9 (_0111, not_13_out, i[2], i[1], i[0]);
  and and_10 (_0110, not_14_out, i[2], i[1], not_15_out);
  and and_11 (_0101, not_16_out, i[2], not_17_out, i[0]);
  and and_12 (_0100, not_18_out, i[2], not_19_out, not_20_out);
  and and_13 (_0011, not_21_out, not_22_out, i[1], i[0]);
  and and_14 (_0010, not_23_out, not_24_out, i[1], not_25_out);
  and and_15 (_0001, not_26_out, not_27_out, not_28_out, i[0]);
  and and_16 (_0000, not_29_out, not_30_out, not_31_out, not_32_out);
endmodule
