// Digital circuit 4x8 Reg File Random.dig as structural Verilog
// 00 - Register 0
// 01 - Register 1
// 10 - Register 3
// 11 - Register 3
module _4x8_Reg_File_Random (
  input  s,
  input  e,
  input  [1:0] rs,
  input  [7:0] i,
  input  c,
  output [7:0] R0,
  output [7:0] R1,
  output [7:0] R2,
  output [7:0] R3,
  output [7:0] o
);

  wire _2_bit_decoder_1__00, _2_bit_decoder_1__01, _2_bit_decoder_1__10, _2_bit_decoder_1__11, and_1_out;
  wire [1:0] not_1_out;
  wire [7:0] _8_bit_switch_1_o, multiplexer_1_out;

  not not_1 (not_1_out[0], rs[0]);
  not not_2 (not_1_out[1], rs[1]);
  and and_1 (and_1_out, c, s);
  _2_Bit_Decoder _2_bit_decoder_1 (
    .i(not_1_out), .e(and_1_out), ._00(_2_bit_decoder_1__00), ._01(_2_bit_decoder_1__01),
    ._10(_2_bit_decoder_1__10), ._11(_2_bit_decoder_1__11));
  _8_Bit_Switch _8_bit_switch_1 (.i(i), .e(s), .o(_8_bit_switch_1_o));
  _1_Byte_Register_Random _1_byte_register_random_1 (.i(_8_bit_switch_1_o), .c(_2_bit_decoder_1__00), .s(1'b1), .o(R3));
  _1_Byte_Register_Random _1_byte_register_random_2 (.i(_8_bit_switch_1_o), .c(_2_bit_decoder_1__01), .s(1'b1), .o(R2));
  _1_Byte_Register_Random _1_byte_register_random_3 (.i(_8_bit_switch_1_o), .c(_2_bit_decoder_1__10), .s(1'b1), .o(R1));
  _1_Byte_Register_Random _1_byte_register_random_4 (.i(_8_bit_switch_1_o), .c(_2_bit_decoder_1__11), .s(1'b1), .o(R0));
  Multiplexer #(.Selector_Bits(2), .Bits(8)) multiplexer_1 (
    .sel(not_1_out), .in_0(R3), .in_1(R2), .in_2(R1), .in_3(R0), .out(multiplexer_1_out));
  _8_Bit_Switch _8_bit_switch_2 (.i(multiplexer_1_out), .e(e), .o(o));

  // Notes on the sheet:
  //   e: opcode input
  //   rs: opcode input
endmodule
