// Digital circuit 8 Bit ALU.dig as structural Verilog
module _8_Bit_ALU (
  input  c_i,
  input  [2:0] op,
  input  [7:0] i_1,
  input  [7:0] i_2,
  output [3:0] flg_o,
  output [7:0] o
);

  wire _8_bit_rca_1_c_o, _8_bit_shift_left_1_s_o, _8_bit_shift_right_1_s_o, alu_decoder_1_p2,
       alu_decoder_1_p3, alu_decoder_1_p4, and_1_out, and_2_out, and_3_out;
  wire [2:0] not_1_out;
  wire [7:0] _8_bit_and_1_o, _8_bit_compare_xor_1_o, _8_bit_inverter_1_o, _8_bit_or_1_o, _8_bit_rca_1_o,
       _8_bit_shift_left_1_o, _8_bit_shift_right_1_o;

  not not_1 (not_1_out[0], op[0]);
  not not_2 (not_1_out[1], op[1]);
  not not_3 (not_1_out[2], op[2]);
  _8_Bit_Compare_XOR _8_bit_compare_xor_1 (
    .i_1(i_1), .i_2(i_2), .o(_8_bit_compare_xor_1_o), .eq(flg_o[0]), .gt(flg_o[1]));
  _8_Bit_OR _8_bit_or_1 (.i_1(i_1), .i_2(i_2), .o(_8_bit_or_1_o));
  _8_Bit_AND _8_bit_and_1 (.i_1(i_1), .i_2(i_2), .o(_8_bit_and_1_o));
  _8_Bit_Inverter _8_bit_inverter_1 (.i(i_1), .o(_8_bit_inverter_1_o));
  _8_Bit_Shift_Right _8_bit_shift_right_1 (
    .s_i(c_i), .i(i_1), .o(_8_bit_shift_right_1_o), .s_o(_8_bit_shift_right_1_s_o));
  _8_Bit_Shift_Left _8_bit_shift_left_1 (.i(i_1), .s_i(c_i), .s_o(_8_bit_shift_left_1_s_o), .o(_8_bit_shift_left_1_o));
  _8_Bit_RCA _8_bit_rca_1 (.c_i(c_i), .i_1(i_1), .i_2(i_2), .o(_8_bit_rca_1_o), .c_o(_8_bit_rca_1_c_o));
  Multiplexer #(.Selector_Bits(3), .Bits(8)) multiplexer_1 (
    .sel(not_1_out), .in_0(_8_bit_compare_xor_1_o), .in_1(_8_bit_or_1_o), .in_2(_8_bit_and_1_o),
    .in_3(_8_bit_inverter_1_o), .in_4(_8_bit_shift_right_1_o), .in_5(_8_bit_shift_left_1_o), .in_6(i_2),
    .in_7(_8_bit_rca_1_o), .out(o));
  // ALU_Decoder alu_decoder_1: pin names not known; wires that end beside it: op, alu_decoder_1_p2, alu_decoder_1_p3, alu_decoder_1_p4
  Zero zero_1 (.op(o), .o(flg_o[2]));
  and and_1 (and_1_out, _8_bit_shift_right_1_s_o, alu_decoder_1_p2);
  and and_2 (and_2_out, _8_bit_shift_left_1_s_o, alu_decoder_1_p3);
  and and_3 (and_3_out, _8_bit_rca_1_c_o, alu_decoder_1_p4);
  or or_1 (flg_o[3], and_1_out, and_2_out, and_3_out);
endmodule
