// Digital circuit Control Unit (new test).dig as structural Verilog
module Control_Unit__new_test (
  input  [3:0] flgs_i,
  input  clk_s,
  input  clk,
  input  clk_e,
  input  [7:0] inst_i,
  output io_s,
  output io_e,
  output io_da,
  output io,
  output flg_s,
  output acc_s,
  output acc_e,
  output alu_c,
  output [2:0] alu_op,
  output b1_e,
  output tmp_s,
  output reg_s,
  output reg_e,
  output [1:0] reg_rs,
  output ram_s,
  output ram_e,
  output mar_s,
  output pc_s,
  output pc_e,
  output inst_s,
  output [2:0] step_dbg
);

  wire _3_bit_decoder_1__000, _3_bit_decoder_1__001, _3_bit_decoder_1__010, _3_bit_decoder_1__011,
       _3_bit_decoder_1__100, _3_bit_decoder_1__101, _3_bit_decoder_1__110, _3_bit_decoder_1__111, and_6_out,
       and_7_out, and_8_out, and_9_out, and_16_out, and_17_out, and_18_out, and_19_out, and_20_out,
       and_21_out, and_22_out, and_23_out, and_24_out, and_25_out, and_26_out, and_27_out, and_28_out,
       and_29_out, and_30_out, and_31_out, and_32_out, and_33_out, and_34_out, and_35_out, and_36_out,
       and_37_out, load_instruction_decoder_1_clr_f, load_instruction_decoder_1_jmp_a,
       load_instruction_decoder_1_jmp_c, load_instruction_decoder_1_jmp_r, load_instruction_decoder_1_ld,
       load_instruction_decoder_1_mov_i, load_instruction_decoder_1_nop, load_instruction_decoder_1_str,
       not_1_out, not_2_out, not_3_out, not_4_out, not_5_out, or_1_out, or_2_out, or_3_out, or_4_out,
       or_6_out, or_7_out, or_8_out, or_9_out, or_10_out, or_11_out, or_12_out, reg_ai, reg_ao, reg_bi,
       reg_bo, reg_rs_t, rs_ff_as_1_q;

  not not_1 (not_1_out, reg_rs_t);
  and and_1 (alu_op[2], inst_i[2], inst_i[3], and_27_out);
  and and_2 (alu_op[1], inst_i[1], inst_i[3], and_27_out);
  and and_3 (alu_op[0], inst_i[0], inst_i[3], and_27_out);
  and and_4 (reg_ao, reg_e, reg_rs_t);
  and and_5 (reg_bo, reg_e, not_1_out);
  Multiplexer #(.Bits(2)) multiplexer_1 (.sel(reg_rs_t), .in_0(inst_i[7:6]), .in_1(inst_i[5:4]), .out(reg_rs));
  not not_2 (not_2_out, inst_i[3]);
  and and_6 (and_6_out, flgs_i[0], inst_i[4]);
  and and_7 (and_7_out, flgs_i[1], inst_i[5]);
  and and_8 (and_8_out, flgs_i[2], inst_i[6]);
  and and_9 (and_9_out, flgs_i[3], inst_i[7]);
  load_instruction_decoder load_instruction_decoder_1 (
    .i(inst_i[2:0]), .e(not_2_out), .clr_f(load_instruction_decoder_1_clr_f),
    .ld(load_instruction_decoder_1_ld), .str(load_instruction_decoder_1_str),
    .mov_i(load_instruction_decoder_1_mov_i), .jmp_r(load_instruction_decoder_1_jmp_r),
    .jmp_a(load_instruction_decoder_1_jmp_a), .jmp_c(load_instruction_decoder_1_jmp_c),
    .nop(load_instruction_decoder_1_nop));
  LED reg_a (.in(reg_ao));
  LED reg_b (.in(reg_bo));
  or or_1 (or_1_out, and_6_out, and_7_out, and_8_out, and_9_out);
  and and_10 (pc_e, or_2_out, clk_e);
  and and_11 (ram_e, or_3_out, clk_e);
  and and_12 (reg_e, or_4_out, clk_e);
  and and_13 (b1_e, or_6_out, clk_e);
  and and_14 (acc_e, or_7_out, clk_e);
  and and_15 (io_e, and_34_out, clk_e);
  and and_16 (and_16_out, load_instruction_decoder_1_jmp_c, or_1_out);
  RS_FF_AS rs_ff_as_1 (.S(clk), .R(1'b0), .Q(rs_ff_as_1_q));  // open: nQ
  not not_3 (not_3_out, clk);
  Counter #(.Bits(3)) step (.en(rs_ff_as_1_q), .C(not_3_out), .clr(1'b0), .out(step_dbg));  // open: ovf
  or or_2 (or_2_out, _3_bit_decoder_1__000, and_21_out, and_23_out, and_24_out);
  or or_3 (or_3_out, _3_bit_decoder_1__001, and_28_out, and_30_out, and_31_out, and_37_out);
  or or_4 (or_4_out, and_17_out, and_19_out, and_20_out, and_22_out, and_26_out, and_27_out, and_29_out);
  or or_5 (reg_rs_t, and_17_out, and_19_out, and_20_out);
  or or_6 (or_6_out, _3_bit_decoder_1__000, and_18_out, and_21_out, and_24_out);
  or or_7 (or_7_out, _3_bit_decoder_1__010, and_32_out, and_35_out, and_36_out);
  and and_17 (and_17_out, _3_bit_decoder_1__011, inst_i[3]);
  and and_18 (and_18_out, _3_bit_decoder_1__011, load_instruction_decoder_1_clr_f);
  and and_19 (and_19_out, _3_bit_decoder_1__011, load_instruction_decoder_1_ld);
  and and_20 (and_20_out, _3_bit_decoder_1__011, load_instruction_decoder_1_str);
  and and_21 (and_21_out, _3_bit_decoder_1__011, load_instruction_decoder_1_mov_i);
  and and_22 (and_22_out, _3_bit_decoder_1__011, load_instruction_decoder_1_jmp_r);
  and and_23 (and_23_out, _3_bit_decoder_1__011, load_instruction_decoder_1_jmp_a);
  and and_24 (and_24_out, _3_bit_decoder_1__011, load_instruction_decoder_1_jmp_c);
  and and_25 (and_25_out, _3_bit_decoder_1__011, load_instruction_decoder_1_nop);
  _3_Bit_Decoder _3_bit_decoder_1 (
    .i(step_dbg), ._111(_3_bit_decoder_1__111), ._110(_3_bit_decoder_1__110), ._101(_3_bit_decoder_1__101),
    ._100(_3_bit_decoder_1__100), ._011(_3_bit_decoder_1__011), ._010(_3_bit_decoder_1__010),
    ._001(_3_bit_decoder_1__001), ._000(_3_bit_decoder_1__000));
  and and_26 (and_26_out, and_25_out, inst_i[4]);
  and and_27 (and_27_out, _3_bit_decoder_1__100, inst_i[3]);
  and and_28 (and_28_out, _3_bit_decoder_1__100, load_instruction_decoder_1_ld);
  and and_29 (and_29_out, _3_bit_decoder_1__100, load_instruction_decoder_1_str);
  and and_30 (and_30_out, _3_bit_decoder_1__100, load_instruction_decoder_1_mov_i);
  and and_31 (and_31_out, _3_bit_decoder_1__100, load_instruction_decoder_1_jmp_a);
  and and_32 (and_32_out, _3_bit_decoder_1__100, load_instruction_decoder_1_jmp_c);
  and and_33 (and_33_out, _3_bit_decoder_1__100, load_instruction_decoder_1_nop);
  not not_4 (not_4_out, inst_i[4]);
  and and_34 (and_34_out, and_33_out, not_4_out);
  and and_35 (and_35_out, _3_bit_decoder_1__101, inst_i[3]);
  and and_36 (and_36_out, _3_bit_decoder_1__101, load_instruction_decoder_1_mov_i);
  and and_37 (and_37_out, _3_bit_decoder_1__101, and_16_out);
  or or_8 (or_8_out, _3_bit_decoder_1__010, and_22_out, and_31_out, and_32_out, and_36_out, and_37_out);
  or or_9 (or_9_out, _3_bit_decoder_1__000, and_19_out, and_20_out, and_21_out, and_23_out, and_24_out);
  or or_10 (or_10_out, and_28_out, and_30_out, and_34_out, and_35_out);
  or or_11 (or_11_out, _3_bit_decoder_1__000, and_21_out, and_24_out, and_27_out);
  or or_12 (or_12_out, and_18_out, and_27_out);
  and and_38 (inst_s, clk_s, _3_bit_decoder_1__001);
  and and_39 (pc_s, clk_s, or_8_out);
  and and_40 (ram_s, clk_s, and_29_out);
  and and_41 (mar_s, clk_s, or_9_out);
  and and_42 (reg_s, clk_s, or_10_out);
  and and_43 (tmp_s, clk_s, and_17_out);
  and and_44 (acc_s, clk_s, or_11_out);
  and and_45 (flg_s, clk_s, or_12_out);
  and and_46 (io_s, clk_s, and_26_out);
  LED reg_a_2 (.in(reg_ai));
  LED reg_b_2 (.in(reg_bi));
  and and_47 (reg_ai, reg_s, reg_rs_t);
  and and_48 (reg_bi, reg_s, not_5_out);
  not not_5 (not_5_out, reg_rs_t);

  assign alu_c = flgs_i[3];
  assign io = inst_i[4];
  assign io_da = inst_i[5];

  // Other names for the same wires on the sheet: reg_i = reg_s; reg_o = reg_e

  // Notes on the sheet:
  //   io_da: data/address
  //   io: data/address
  //   alu
  //   clr_f
  //   load
  //   store
  //   mov_i
  //   jump_r
  //   jump_a
  //   jmp_c
  //   io
endmodule
