// Digital circuit EEPROM.dig as structural Verilog
module EEPROM (
  input  s_d,
  input  e,
  input  [7:0] i_a,
  input  [7:0] i_d,
  input  clk,
  output [7:0] o
);

  EEPROMDualPort #(.AddrBits(8), .Bits(8)) eepromdualport_1 (.A(i_a), .Din(i_d), .str(s_d), .C(clk), .ld(e), .D(o));

  // Notes on the sheet:
  //   s_d: store data
  //   e: enable out
  //   i_a: address in
  //   i_d: data in
  //   contents of eepromdualport_1 (hex, n*v repeats v):
  //   3,8*0,9
endmodule
