// Digital circuit Memory Address Register.dig as structural Verilog
module Memory_Address_Register (
  input  s,
  input  [7:0] i,
  input  clk,
  output [7:0] o
);

  wire and_1_out;

  and and_1 (and_1_out, clk, s);
  _1_Byte_Memory _1_byte_memory_1 (.i(i), .c(and_1_out), .o(o));
endmodule
