// Digital circuit Program Counter.dig as structural Verilog
module Program_Counter (
  input  s,
  input  e_o,
  input  [7:0] i,
  input  clk,
  output [7:0] o_dbg,
  output [7:0] o
);

  _1_Byte_Register _1_byte_register_1 (.i(i), .clk(clk), .s(s), .o(o_dbg));
  _8_Bit_Switch _8_bit_switch_1 (.i(o_dbg), .e(e_o), .o(o));

  // Notes on the sheet:
  //   s: enable store
  //   e_o: enable out
  //   i: in
endmodule
