// Digital circuit op reader.dig as structural Verilog
module op_reader (
  input  [7:0] op,
  output XOR,
  output OR,
  output AND,
  output NOT,
  output SHL,
  output SHR,
  output ADD,
  output CMP
);

  wire and_1_out, and_2_out, and_3_out, and_4_out, and_5_out, and_6_out, and_7_out, and_8_out, not_1_out,
       not_2_out, not_3_out, not_4_out, not_5_out, not_6_out, not_7_out, not_8_out, not_9_out, not_10_out,
       not_11_out, not_12_out;

  not not_1 (not_1_out, op[1]);
  not not_2 (not_2_out, op[2]);
  not not_3 (not_3_out, op[2]);
  not not_4 (not_4_out, op[1]);
  not not_5 (not_5_out, op[3]);
  not not_6 (not_6_out, op[3]);
  not not_7 (not_7_out, op[1]);
  not not_8 (not_8_out, op[3]);
  not not_9 (not_9_out, op[2]);
  not not_10 (not_10_out, op[3]);
  not not_11 (not_11_out, op[2]);
  not not_12 (not_12_out, op[1]);
  and and_1 (and_1_out, op[3], op[2], op[1]);
  and and_2 (and_2_out, op[3], op[2], not_1_out);
  and and_3 (and_3_out, op[3], not_2_out, op[1]);
  and and_4 (and_4_out, op[3], not_3_out, not_4_out);
  and and_5 (and_5_out, not_5_out, op[2], op[1]);
  and and_6 (and_6_out, not_6_out, op[2], not_7_out);
  and and_7 (and_7_out, not_8_out, not_9_out, op[1]);
  and and_8 (and_8_out, not_10_out, not_11_out, not_12_out);
  _1_Bit_Switch _1_bit_switch_1 (.i(and_1_out), .e(op[0]), .o(XOR));
  _1_Bit_Switch _1_bit_switch_2 (.i(and_2_out), .e(op[0]), .o(OR));
  _1_Bit_Switch _1_bit_switch_3 (.i(and_3_out), .e(op[0]), .o(AND));
  _1_Bit_Switch _1_bit_switch_4 (.i(and_4_out), .e(op[0]), .o(NOT));
  _1_Bit_Switch _1_bit_switch_5 (.i(and_5_out), .e(op[0]), .o(SHL));
  _1_Bit_Switch _1_bit_switch_6 (.i(and_6_out), .e(op[0]), .o(SHR));
  _1_Bit_Switch _1_bit_switch_7 (.i(and_7_out), .e(op[0]), .o(ADD));
  _1_Bit_Switch _1_bit_switch_8 (.i(and_8_out), .e(op[0]), .o(CMP));
endmodule
