// Digital circuit 1 Bit Memory (fix).dig as structural Verilog
module _1_Bit_Memory__fix (
  input  s,
  input  c,
  output o
);

  wire and_1_out, and_2_out, delay_1_out, nor_1_out, not_1_out, or_1_out, pulser_1_o;

  not not_1 (not_1_out, s);
  and and_1 (and_1_out, s, c);
  and and_2 (and_2_out, c, not_1_out);
  nor nor_1 (nor_1_out, and_1_out, o);
  nor nor_2 (o, or_1_out, and_2_out);
  Delay #(.delayTime(20)) delay_1 (.in(1'b1), .out(delay_1_out));
  Pulser pulser_1 (.c(delay_1_out), .o(pulser_1_o));
  or or_1 (or_1_out, pulser_1_o, nor_1_out);
endmodule
