// Digital circuit 1 Bit Memory.dig as structural Verilog
module _1_Bit_Memory (
  input  s,
  input  c,
  output o
);

  wire and_1_out, and_2_out, nor_1_out, not_1_out;

  not not_1 (not_1_out, s);
  and and_1 (and_1_out, s, c);
  and and_2 (and_2_out, c, not_1_out);
  nor nor_1 (nor_1_out, and_1_out, o);
  nor nor_2 (o, nor_1_out, and_2_out);
endmodule
