// Digital circuit 1 Byte Memory Random.dig as structural Verilog
module _1_Byte_Memory_Random (
  input  [7:0] i,
  input  c,
  output [7:0] o
);

  _1_Bit_Memory _1_bit_memory_1 (.s(i[0]), .c(c), .o(o[0]));
  _1_Bit_Memory _1_bit_memory_2 (.s(i[1]), .c(c), .o(o[1]));
  _1_Bit_Memory _1_bit_memory_3 (.s(i[2]), .c(c), .o(o[2]));
  _1_Bit_Memory _1_bit_memory_4 (.s(i[3]), .c(c), .o(o[3]));
  _1_Bit_Memory _1_bit_memory_5 (.s(i[4]), .c(c), .o(o[4]));
  _1_Bit_Memory _1_bit_memory_6 (.s(i[5]), .c(c), .o(o[5]));
  _1_Bit_Memory _1_bit_memory_7 (.s(i[6]), .c(c), .o(o[6]));
  _1_Bit_Memory _1_bit_memory_8 (.s(i[7]), .c(c), .o(o[7]));
endmodule
