// Digital circuit 1 Byte Memory.dig as structural Verilog
module _1_Byte_Memory (
  input  [7:0] i,
  input  c,
  output [7:0] o
);

  _1_Bit_Memory__fix _1_bit_memory__fix_1 (.s(i[0]), .c(c), .o(o[0]));
  _1_Bit_Memory__fix _1_bit_memory__fix_2 (.s(i[1]), .c(c), .o(o[1]));
  _1_Bit_Memory__fix _1_bit_memory__fix_3 (.s(i[2]), .c(c), .o(o[2]));
  _1_Bit_Memory__fix _1_bit_memory__fix_4 (.s(i[3]), .c(c), .o(o[3]));
  _1_Bit_Memory__fix _1_bit_memory__fix_5 (.s(i[4]), .c(c), .o(o[4]));
  _1_Bit_Memory__fix _1_bit_memory__fix_6 (.s(i[5]), .c(c), .o(o[5]));
  _1_Bit_Memory__fix _1_bit_memory__fix_7 (.s(i[6]), .c(c), .o(o[6]));
  _1_Bit_Memory__fix _1_bit_memory__fix_8 (.s(i[7]), .c(c), .o(o[7]));
endmodule
