// Digital circuit 1 Byte Register Random.dig as structural Verilog
module _1_Byte_Register_Random (
  input  [7:0] i,
  input  c,
  input  s,
  output [7:0] o
);

  wire and_1_out;

  and and_1 (and_1_out, c, s);
  _1_Byte_Memory_Random _1_byte_memory_random_1 (.i(i), .c(and_1_out), .o(o));
endmodule
