// Digital circuit 1 Byte Register Switch.dig as structural Verilog
module _1_Byte_Register_Switch (
  input  [7:0] i,
  input  c,
  input  e,
  input  ld,
  output [7:0] o
);

  wire and_1_out;
  wire [7:0] _1_byte_memory_1_o;

  and and_1 (and_1_out, c, ld);
  _1_Byte_Memory _1_byte_memory_1 (.i(i), .c(and_1_out), .o(_1_byte_memory_1_o));
  _8_Bit_Switch _8_bit_switch_1 (.i(_1_byte_memory_1_o), .e(e), .o(o));
endmodule
