// Digital circuit 1 Byte Gate.dig as structural Verilog
module _1_Byte_Gate (
  input  [7:0] i,
  input  en,
  output [7:0] o
);

  and and_1 (o[0], i[0], en);
  and and_2 (o[1], i[1], en);
  and and_3 (o[2], i[2], en);
  and and_4 (o[3], i[3], en);
  and and_5 (o[4], i[4], en);
  and and_6 (o[5], i[5], en);
  and and_7 (o[6], i[6], en);
  and and_8 (o[7], i[7], en);
endmodule
