// Digital circuit 1 Cycle Flag.dig as structural Verilog
module _1_Cycle_Flag (
  input  c,
  input  s,
  output o
);

  wire and_1_out, and_2_out, or_1_out;

  and and_1 (and_1_out, c, s);
  and and_2 (and_2_out, o, c);
  or or_1 (or_1_out, and_2_out, and_1_out);
  Falling_Edge_Flip_Flop falling_edge_flip_flop_1 (.c(or_1_out), .o(o));
endmodule
