// Digital circuit 2x8 Demux.dig as structural Verilog
module _2x8_Demux (
  input  [7:0] i2,
  input  en,
  input  [7:0] i1,
  output [7:0] o
);

  wire not_1_out;

  and and_1 (o[0], i1[0], not_1_out);
  and and_2 (o[1], i1[1], not_1_out);
  and and_3 (o[2], i1[2], not_1_out);
  and and_4 (o[3], i1[3], not_1_out);
  and and_5 (o[4], i1[4], not_1_out);
  and and_6 (o[5], i1[5], not_1_out);
  and and_7 (o[6], i1[6], not_1_out);
  and and_8 (o[7], i1[7], not_1_out);
  not not_1 (not_1_out, en);
  and and_9 (o[0], i2[0], en);
  and and_10 (o[1], i2[1], en);
  and and_11 (o[2], i2[2], en);
  and and_12 (o[3], i2[3], en);
  and and_13 (o[4], i2[4], en);
  and and_14 (o[5], i2[5], en);
  and and_15 (o[6], i2[6], en);
  and and_16 (o[7], i2[7], en);
endmodule
