// Digital circuit Check for Clear.dig as structural Verilog
module Check_for_Clear (
  input  [7:0] op,
  output o
);

  wire not_1_out, not_2_out, or_1_out, or_2_out, or_3_out, or_4_out, or_5_out, or_6_out, or_7_out;

  not not_1 (not_1_out, op[1]);
  not not_2 (not_2_out, op[2]);
  or or_1 (or_1_out, op[0], not_1_out);
  or or_2 (or_2_out, or_1_out, not_2_out);
  or or_3 (or_3_out, or_2_out, op[3]);
  or or_4 (or_4_out, or_3_out, op[4]);
  or or_5 (or_5_out, or_4_out, op[5]);
  or or_6 (or_6_out, or_5_out, op[6]);
  or or_7 (or_7_out, or_6_out, op[7]);
  not not_3 (o, or_7_out);
endmodule
