// Digital circuit Falling Edge Flip Flop.dig as structural Verilog
module Falling_Edge_Flip_Flop (
  input  c,
  output o
);

  wire not_1_out, not_2_out, pulser_1_o;

  not not_1 (not_1_out, c);
  Pulser pulser_1 (.c(not_1_out), .o(pulser_1_o));
  _1_Bit_Memory _1_bit_memory_1 (.s(not_2_out), .c(pulser_1_o), .o(o));
  not not_2 (not_2_out, o);
endmodule
