// Digital circuit Falling Edge Test.dig as structural Verilog
module Falling_Edge_Test (
  input  c,
  output o
);

  wire not_1_out;

  not not_1 (not_1_out, c);
  Pulser pulser_1 (.c(not_1_out), .o(o));
endmodule
