// Digital circuit Pulser.dig as structural Verilog
module Pulser (
  input  c,
  output o
);

  wire not_1_out, not_2_out, not_3_out;

  not not_1 (not_1_out, c);
  not not_2 (not_2_out, not_1_out);
  not not_3 (not_3_out, not_2_out);
  and and_1 (o, not_3_out, c);
endmodule
