// Digital circuit inst decoder TEST.dig as structural Verilog
module inst_decoder_TEST (
);

  wire _3_bit_decoder_1__000, _3_bit_decoder_1__001, _3_bit_decoder_1__010, _3_bit_decoder_1__011,
       _3_bit_decoder_1__100, _3_bit_decoder_1__101, _3_bit_decoder_1__110, _3_bit_decoder_1__111, and_1_out,
       and_2_out, and_3_out, and_4_out, and_5_out, and_6_out, and_7_out, and_8_out, and_9_out, and_10_out,
       and_11_out, and_12_out, and_13_out, and_14_out, and_15_out, and_16_out, not_1_out, undriven;

  and and_1 (and_1_out, _3_bit_decoder_1__001, undriven);
  and and_2 (and_2_out, _3_bit_decoder_1__000, undriven);
  and and_3 (and_3_out, _3_bit_decoder_1__010, undriven);
  _3_Bit_Decoder _3_bit_decoder_1 (
    ._111(_3_bit_decoder_1__111), ._110(_3_bit_decoder_1__110), ._101(_3_bit_decoder_1__101),
    ._100(_3_bit_decoder_1__100), ._011(_3_bit_decoder_1__011), ._010(_3_bit_decoder_1__010),
    ._001(_3_bit_decoder_1__001), ._000(_3_bit_decoder_1__000));  // open: i
  and and_4 (and_4_out, _3_bit_decoder_1__011, undriven);
  and and_5 (and_5_out, _3_bit_decoder_1__101, undriven);
  and and_6 (and_6_out, _3_bit_decoder_1__100, undriven);
  and and_7 (and_7_out, _3_bit_decoder_1__110, undriven);
  not not_1 (not_1_out, undriven);
  and and_8 (and_8_out, _3_bit_decoder_1__111, undriven);
  and and_9 (and_9_out, _3_bit_decoder_1__000, not_1_out);
  and and_10 (and_10_out, _3_bit_decoder_1__001, not_1_out);
  and and_11 (and_11_out, _3_bit_decoder_1__010, not_1_out);
  and and_12 (and_12_out, _3_bit_decoder_1__100, not_1_out);
  and and_13 (and_13_out, _3_bit_decoder_1__011, not_1_out);
  and and_14 (and_14_out, _3_bit_decoder_1__101, not_1_out);
  and and_15 (and_15_out, _3_bit_decoder_1__110, not_1_out);
  and and_16 (and_16_out, _3_bit_decoder_1__111, not_1_out);
endmodule
