// Digital circuit IO File.dig as structural Verilog
module IO_File (
  input  [7:0] addr_i,
  input  [3:0] io_i,
  output [4:0] dis,
  output [4:0] kb
);

  wire not_1_out, not_2_out, not_3_out, not_4_out, not_5_out, not_6_out, not_7_out, not_8_out, not_9_out,
       not_10_out, not_11_out, not_12_out, not_13_out, not_14_out;

  not not_1 (not_1_out, addr_i[7]);
  not not_2 (not_2_out, addr_i[6]);
  not not_3 (not_3_out, addr_i[5]);
  not not_4 (not_4_out, addr_i[4]);
  not not_5 (not_5_out, addr_i[3]);
  not not_6 (not_6_out, addr_i[2]);
  not not_7 (not_7_out, addr_i[0]);
  not not_8 (not_8_out, addr_i[7]);
  not not_9 (not_9_out, addr_i[6]);
  not not_10 (not_10_out, addr_i[5]);
  not not_11 (not_11_out, addr_i[4]);
  not not_12 (not_12_out, addr_i[3]);
  not not_13 (not_13_out, addr_i[2]);
  not not_14 (not_14_out, addr_i[1]);
  and and_1 (dis[0], not_1_out, not_2_out, not_3_out, not_4_out, not_5_out, not_6_out, addr_i[1], not_7_out);
  and and_2 (kb[0], not_8_out, not_9_out, not_10_out, not_11_out, not_12_out, not_13_out, not_14_out, addr_i[0]);

  assign dis[4:1] = io_i;
  assign kb[4:1] = io_i;
endmodule
