// Digital circuit Keyboard.dig as structural Verilog
module Keyboard (
  input  [4:0] io,
  output [7:0] o
);

  wire _1_bit_memory__fix_1_o, and_1_out, and_2_out, and_3_out, not_1_out, not_2_out, not_3_out, not_4_out,
       not_5_out;
  wire [15:8] keyboard_1_d;

  not not_1 (not_1_out, io[3]);
  not not_2 (not_2_out, io[4]);
  and and_1 (and_1_out, io[2], not_1_out, not_2_out);
  and and_2 (and_2_out, io[1], io[3], io[4]);
  _1_Bit_Memory__fix _1_bit_memory__fix_1 (.s(io[0]), .c(and_2_out), .o(_1_bit_memory__fix_1_o));
  and and_3 (and_3_out, and_1_out, _1_bit_memory__fix_1_o);
  not not_3 (not_3_out, and_3_out);
  not not_4 (not_4_out, and_3_out);
  not not_5 (not_5_out, not_4_out);
  Keyboard keyboard_1 (.C(not_3_out), .en(not_5_out), .D({keyboard_1_d, o}));  // open: av
endmodule
