// Digital circuit ds1.dig as structural Verilog
module ds1 (
  input  [15:0] res,
  input  clk,
  input  [9:0] fp,
  input  [9:0] sync,
  input  [9:0] bp,
  input  en,
  output [15:0] V,
  output sync_2,
  output next
);

  wire [15:0] sub_1_s;

  Sub #(.Bits(16)) sub_1 (.a(res), .b(16'h1), .c_i(1'b0), .s(sub_1_s));  // open: c_o
  Comparator #(.Bits(16)) comparator_1 (.a(V), .b(sub_1_s), .eq(next));  // open: gt, lt
  CounterPreset #(.Bits(16)) counterpreset_1 (
    .en(en), .C(clk), .dir(1'b0), .in(16'hfff6), .ld(next), .clr(1'b0), .out(V));  // open: ovf

  assign sync_2 = next;

  // Notes on the sheet:
  //   res: default 640
  //   fp: default 16
  //   sync: default 96
  //   bp: default 48
endmodule
