// Digital circuit 1 Bit Switch.dig as structural Verilog
module _1_Bit_Switch (
  input  i,
  input  e,
  output o
);

  // Relay relay_1: pin names not known; wires that end beside it: i, e, o, 1'b0
endmodule
