// Digital circuit 3 Bit Switch.dig as structural Verilog
module _3_Bit_Switch (
  input  [2:0] i,
  input  e,
  output [2:0] o
);

  // Relay #(.Bits(3)) relay_1: pin names not known; wires that end beside it: i, e, o, 1'b0
endmodule
