// Digital circuit 4 Bit Switch.dig as structural Verilog
module _4_Bit_Switch (
  input  [3:0] i,
  input  e,
  output [3:0] o
);

  // Relay #(.Bits(4)) relay_1: pin names not known; wires that end beside it: i, e, o, 1'b0
endmodule
