// Digital circuit 8 Bit Switch.dig as structural Verilog
module _8_Bit_Switch (
  input  [7:0] i,
  input  e,
  output [7:0] o
);

  // Relay #(.Bits(8)) relay_1: pin names not known; wires that end beside it: i, e, o, 1'b0
endmodule
