// Digital circuit df8.dig as structural Verilog
module df8 (
  input  clock,
  output [7:0] R0,
  output [7:0] R1,
  output [7:0] R2,
  output [7:0] R3,
  output [7:0] PC,
  output [2:0] step
);

  wire c, control_unit_1_acc_e, control_unit_1_acc_s, control_unit_1_alu_c, control_unit_1_b1_e,
       control_unit_1_flg_s, control_unit_1_inst_s, control_unit_1_mar_s, control_unit_1_pc_e,
       control_unit_1_pc_s, control_unit_1_ram_e, control_unit_1_ram_s, control_unit_1_reg_e,
       control_unit_1_reg_s, control_unit_1_tmp_s, eq, gt, z;
  wire [1:0] control_unit_1_reg_rs;
  wire [2:0] control_unit_1_alu_op;
  wire [3:0] _8_bit_alu_1_flg_o, control_unit_1_io;
  wire [4:0] io_file_1_dis, io_file_1_kb;
  wire [7:0] _8_bit_alu_1_o, bus_1_1_o, instruction_register_1_o, memory_address_register_1_o,
       program_counter_1_o, tmp_1_o;

  IO_File io_file_1 (.addr_i(program_counter_1_o), .io_i(control_unit_1_io), .dis(io_file_1_dis), .kb(io_file_1_kb));
  Control_Unit control_unit_1 (
    .flgs_i({c, z, gt, eq}), .clk(clock), .inst_i(instruction_register_1_o), .IO(control_unit_1_io),
    .flg_s(control_unit_1_flg_s), .acc_s(control_unit_1_acc_s), .acc_e(control_unit_1_acc_e),
    .alu_c(control_unit_1_alu_c), .alu_op(control_unit_1_alu_op), .b1_e(control_unit_1_b1_e),
    .tmp_s(control_unit_1_tmp_s), .reg_s(control_unit_1_reg_s), .reg_e(control_unit_1_reg_e),
    .reg_rs(control_unit_1_reg_rs), .ram_s(control_unit_1_ram_s), .ram_e(control_unit_1_ram_e),
    .mar_s(control_unit_1_mar_s), .pc_s(control_unit_1_pc_s), .pc_e(control_unit_1_pc_e),
    .inst_s(control_unit_1_inst_s), .step_dbg(step));
  Instruction_Register instruction_register_1 (
    .i(program_counter_1_o), .clk(clock), .s(control_unit_1_inst_s), .o(instruction_register_1_o));
  Program_Counter program_counter_1 (
    .s(control_unit_1_pc_s), .e_o(control_unit_1_pc_e), .i(program_counter_1_o), .clk(clock), .o_dbg(PC),
    .o(program_counter_1_o));
  Memory_Address_Register memory_address_register_1 (
    .s(control_unit_1_mar_s), .i(program_counter_1_o), .clk(clock), .o(memory_address_register_1_o));
  EEPROMDualPort #(.AddrBits(8), .isProgramMemory("true"), .Bits(8)) eepromdualport_1 (
    .A(memory_address_register_1_o), .Din(program_counter_1_o), .str(control_unit_1_ram_s), .C(clock),
    .ld(control_unit_1_ram_e), .D(program_counter_1_o));
  _4x8_Reg_File _4x8_reg_file_1 (
    .s(control_unit_1_reg_s), .e(control_unit_1_reg_e), .rs(control_unit_1_reg_rs), .i(program_counter_1_o),
    .c(clock), .R0(R0), .R1(R1), .R2(R2), .R3(R3), .o(program_counter_1_o));
  TMP tmp_1 (.s(control_unit_1_tmp_s), .i(program_counter_1_o), .clk(clock), .o(tmp_1_o));
  Bus_1 bus_1_1 (.e(control_unit_1_b1_e), .i(tmp_1_o), .o(bus_1_1_o));
  _8_Bit_ALU _8_bit_alu_1 (
    .c_i(control_unit_1_alu_c), .op(control_unit_1_alu_op), .i_1(bus_1_1_o), .i_2(program_counter_1_o),
    .flg_o(_8_bit_alu_1_flg_o), .o(_8_bit_alu_1_o));
  Flags flags_1 (.s(control_unit_1_flg_s), .i(_8_bit_alu_1_flg_o), .clk(clock), .o({c, z, gt, eq}));
  Accumulator accumulator_1 (
    .s(control_unit_1_acc_s), .e(control_unit_1_acc_e), .i(_8_bit_alu_1_o), .clk(clock),
    .o(program_counter_1_o));

  // Other names for the same wires on the sheet: stp[2:0] = step

  // Notes on the sheet:
  //   clock: Hz: 200
  //   contents of eepromdualport_1 (hex, n*v repeats v):
  //   43,0,83,1,c3,e9,0,b9,16,12,f,1e,5f,6e,0,88,5,6,5,12
endmodule
